// Logisim project CPU Test.circ as structural Verilog: 6 circuits, main circuit main
module main (
);

  wire address_mapper_1_re_out, address_mapper_3_re_out, address_mapper_4_we_out, address_mapper_5_re_out,
       address_mapper_5_we_out, address_mapper_6_we_out, address_mapper_7_re_out, address_mapper_7_we_out,
       address_mapper_8_re_out, clock_2_out, clock_3_out, clock_4_out, clock_5_out, clock_6_out, DBG_RESUME,
       demultiplexer_1_out1, demultiplexer_1_out2, demultiplexer_2_out0, demultiplexer_2_out1,
       demultiplexer_2_out2, INT_BUTTON, INT_JOYSTICK, INT_KEYBOARD, INTERRUPT, not_1_out, RE, RESET,
       rgb_video_1_p2, rgb_video_1_p3, WE;
  wire [2:0] bit_extender_3_out;
  wire [7:0] bit_extender_1_out, keyboard_1_data;
  wire [12:0] bit_extender_4_out, JOY_DATA;
  wire [15:0] ADDR, bit_extender_2_out, DATA, HEX_OUT, PAGE, rom_1_data;
  wire [19:0] BCD_OUT;

  Joystick #(.bits(5)) joystick_1 (.x(JOY_DATA[4:0]), .y(JOY_DATA[12:8]));
  _7_Segment_Display u_7_segment_display_1 ();  // open: g, f, a, b, e, d, c, dp
  // Hex_to_7_Segment_decoder hex_to_7_segment_decoder_1: pin names not known
  DotMatrix #(.dotshape("circle"), .matrixcols(16), .matrixrows(1)) dotmatrix_1 (
    .col0(HEX_OUT[15]), .col1(HEX_OUT[14]), .col2(HEX_OUT[13]), .col3(HEX_OUT[12]), .col4(HEX_OUT[11]),
    .col5(HEX_OUT[10]), .col6(HEX_OUT[9]), .col7(HEX_OUT[8]), .col8(HEX_OUT[7]), .col9(HEX_OUT[6]),
    .col10(HEX_OUT[5]), .col11(HEX_OUT[4]), .col12(HEX_OUT[3]), .col13(HEX_OUT[2]), .col14(HEX_OUT[1]),
    .col15(HEX_OUT[0]));
  _7_Segment_Display u_7_segment_display_2 ();  // open: g, f, a, b, e, d, c, dp
  _7_Segment_Display u_7_segment_display_3 ();  // open: g, f, a, b, e, d, c, dp
  // Hex_to_7_Segment_decoder hex_to_7_segment_decoder_2: pin names not known
  // Hex_to_7_Segment_decoder hex_to_7_segment_decoder_3: pin names not known
  // RGB_Video #(.cursor("No Cursor")) rgb_video_1: pin names not known; wires that end beside it: RESET, rgb_video_1_p2, rgb_video_1_p3, ADDR[6:0], ADDR[13:7], DATA
  Clock clock_1 (.out(rgb_video_1_p2));
  Address_Mapper address_mapper_1 (
    .RE_OUT(address_mapper_1_re_out), .Base({16{1'b0}}), .Mask({16{1'b1}}), .Address(PAGE), .RE_IN(RE));  // open: WE_OUT, WE_IN
  _7_Segment_Display u_7_segment_display_4 ();  // open: g, f, a, b, e, d, c, dp
  // Hex_to_7_Segment_decoder hex_to_7_segment_decoder_4: pin names not known
  Button u_interrupt (.out(INT_BUTTON));
  Button debug_resume (.out(DBG_RESUME));
  Button u_reset (.out(RESET));
  _7_Segment_Display u_7_segment_display_5 ();  // open: g, f, a, b, e, d, c, dp
  _7_Segment_Display u_7_segment_display_6 ();  // open: g, f, a, b, e, d, c, dp
  // BCD_to_7_Segment_decoder bcd_to_7_segment_decoder_1: pin names not known
  // BCD_to_7_Segment_decoder bcd_to_7_segment_decoder_2: pin names not known
  Address_Mapper address_mapper_2 (
    .RE_OUT(rgb_video_1_p3), .Base(16'h8000), .Mask(16'hc000), .Address(ADDR), .RE_IN(address_mapper_1_re_out));  // open: WE_OUT, WE_IN
  _7_Segment_Display u_7_segment_display_7 ();  // open: g, f, a, b, e, d, c, dp
  // BCD_to_7_Segment_decoder bcd_to_7_segment_decoder_3: pin names not known
  _7_Segment_Display u_7_segment_display_8 ();  // open: g, f, a, b, e, d, c, dp
  _7_Segment_Display u_7_segment_display_9 ();  // open: g, f, a, b, e, d, c, dp
  // BCD_to_7_Segment_decoder bcd_to_7_segment_decoder_4: pin names not known
  // BCD_to_7_Segment_decoder bcd_to_7_segment_decoder_5: pin names not known
  Bit_Extender #(.in_width(16), .out_width(8), .\type ("zero")) bit_extender_1 (.in(DATA), .out(bit_extender_1_out));
  TTY #(.asciiwidth(8), .cols(120), .rows(32)) tty_1 (
    .data(bit_extender_1_out[6:0]), .clk(clock_2_out), .we(address_mapper_4_we_out), .clr(RESET));
  Clock clock_2 (.out(clock_2_out));
  Clock clock_3 (.out(clock_3_out));
  Keyboard #(.asciiwidth(8)) keyboard_1 (
    .clk(clock_3_out), .re(1'b1), .clr(RESET), .avail(INT_KEYBOARD), .data(keyboard_1_data[6:0]));
  Address_Mapper address_mapper_3 (
    .RE_OUT(address_mapper_3_re_out), .Base(16'h7f01), .Mask({16{1'b1}}), .Address(ADDR), .WE_IN(WE),
    .RE_IN(RE));  // open: WE_OUT
  Address_Mapper address_mapper_4 (
    .WE_OUT(address_mapper_4_we_out), .Base(16'h7f00), .Mask({16{1'b1}}), .Address(ADDR), .WE_IN(WE),
    .RE_IN(RE));  // open: RE_OUT
  assign bit_extender_2_out = {{8{1'b0}}, keyboard_1_data};  // Bit_Extender bit_extender_2
  assign DATA = address_mapper_3_re_out ? bit_extender_2_out : 16'bz;  // Controlled_Buffer controlled_buffer_1
  Bit_Extender #(.in_width(16), .out_width(3), .\type ("zero")) bit_extender_3 (.in(ADDR), .out(bit_extender_3_out));
  Address_Mapper address_mapper_5 (
    .WE_OUT(address_mapper_5_we_out), .RE_OUT(address_mapper_5_re_out), .Base(16'h7ff0), .Mask(16'hfff8),
    .Address(ADDR), .WE_IN(WE), .RE_IN(RE));
  CH016M01 ch016m01_1 (
    .TO_RAM(DATA), .TO_ADDR(ADDR), .RAM_WE(WE), .RAM_RE(RE), .FROM_RAM(DATA), .INT(INTERRUPT),
    .resume(DBG_RESUME), .CLR(RESET));  // open: STEP_1
  Interrupt_Manager interrupt_manager_1 (
    .Data_Out(DATA), .Interrupt(INTERRUPT), .Source_5(1'b0), .Source_6(1'b0), .Source_7(1'b0),
    .Source_8(1'b0), .Source_9(1'b0), .Source_1(INT_BUTTON), .Source_10(1'b0), .Source_11(1'b0),
    .Source_12(1'b0), .Source_13(1'b0), .Source_14(1'b0), .Source_15(1'b0), .Source_2(INT_JOYSTICK),
    .Source_3(INT_KEYBOARD), .Source_4(1'b0), .Data_In(DATA), .RE(address_mapper_5_re_out),
    .WE(address_mapper_5_we_out), .Register_Select(bit_extender_3_out), .Reset(RESET));
  Clock clock_4 (.out(clock_4_out));
  not not_1 (not_1_out, ADDR[15]);
  Demultiplexer #(.select(2)) demultiplexer_1 (
    .out1(demultiplexer_1_out1), .out2(demultiplexer_1_out2), .in(WE), .sel(ADDR[14:13]), .en(not_1_out));  // open: out0, out3
  Demultiplexer #(.select(2)) demultiplexer_2 (
    .out0(demultiplexer_2_out0), .out1(demultiplexer_2_out1), .out2(demultiplexer_2_out2), .in(RE),
    .sel(ADDR[14:13]), .en(not_1_out));  // open: out3
  Register #(.width(16)) register_1 (
    .D(DATA), .en(address_mapper_6_we_out), .clk(clock_4_out), .Q(HEX_OUT), .clr(RESET));
  ROM #(.addrWidth(13), .dataWidth(16)) rom_1 (.addr(bit_extender_4_out), .data(rom_1_data));
  Bit_Extender #(.in_width(16), .out_width(13), .\type ("zero")) bit_extender_4 (.in(ADDR), .out(bit_extender_4_out));
  RAM #(.addrWidth(13), .dataWidth(16), .databus("bidir")) ram_1 (
    .addr(bit_extender_4_out), .data(DATA));  // open: we, oe, clk
  RAM #(.addrWidth(13), .dataWidth(16), .databus("bidir")) ram_2 (
    .addr(bit_extender_4_out), .data(DATA));  // open: we, oe, clk
  Clock clock_5 (.out(clock_5_out));
  Address_Mapper address_mapper_6 (
    .WE_OUT(address_mapper_6_we_out), .Base(16'h7ffe), .Mask({16{1'b1}}), .Address(ADDR), .WE_IN(WE),
    .RE_IN(RE));  // open: RE_OUT
  Binary_to_BCD binary_to_bcd_1 (
    .Input(DATA), .Load_Start(address_mapper_6_we_out), .Reset(RESET), ._10_000s(BCD_OUT[19:16]),
    ._1_000s(BCD_OUT[15:12]), ._100s(BCD_OUT[11:8]), ._10s(BCD_OUT[7:4]), ._1s(BCD_OUT[3:0]));
  assign DATA = demultiplexer_2_out0 ? rom_1_data : 16'bz;  // Controlled_Buffer controlled_buffer_2
  Address_Mapper address_mapper_7 (
    .WE_OUT(address_mapper_7_we_out), .RE_OUT(address_mapper_7_re_out), .Base(16'h7fff), .Mask({16{1'b1}}),
    .Address(ADDR), .WE_IN(WE), .RE_IN(RE));
  Clock clock_6 (.out(clock_6_out));
  Address_Mapper address_mapper_8 (
    .RE_OUT(address_mapper_8_re_out), .Base(16'h7f02), .Mask({16{1'b1}}), .Address(ADDR), .RE_IN(RE));  // open: WE_OUT, WE_IN
  Register #(.width(16)) register_2 (.D(DATA), .en(address_mapper_7_we_out), .clk(clock_6_out), .Q(PAGE), .clr(RESET));
  Joystick_Processor joystick_processor_1 (
    .Data_Out(DATA), .Interrupt(INT_JOYSTICK), .Data_In({3'b000, JOY_DATA[12:8], 3'b000, JOY_DATA[4:0]}),
    .Reset(RESET), .RE(address_mapper_8_re_out));
  assign DATA = address_mapper_7_re_out ? PAGE : 16'bz;  // Controlled_Buffer controlled_buffer_3
  _7_Segment_Display u_7_segment_display_10 ();  // open: g, f, a, b, e, d, c, dp
  // BCD_to_7_Segment_decoder bcd_to_7_segment_decoder_6: pin names not known
  // Pins of 7 and 8 bits meet at bit_extender_1_out
  // Pins of 7 and 8 bits meet at keyboard_1_data

  // Notes on the sheet:
  //   Joystick
  //   RGB Display
  //   Misc. Inputs
  //   Output Register Display
  //   Keyboard
  //   Terminal Display
  //   Interrupt Manager
  //   Central Processing Unit
  //   Output Register
  //   Main Memory
  //   Page Register
  //   Joystick Handler
endmodule

module Address_Mapper (
  input  [15:0] Base,
  input  [15:0] Mask,
  input  [15:0] Address,
  input  WE_IN,
  input  RE_IN,
  output WE_OUT,
  output RE_OUT
);

  wire comparator_1_eq;
  wire [15:0] and_1_out;

  assign and_1_out = Mask & Address;  // AND_Gate and_1, 16 bits wide
  Comparator #(.mode("unsigned"), .width(16)) comparator_1 (
    .a(Base), .b(and_1_out), .eq(comparator_1_eq));  // open: gt, lt
  and and_2 (WE_OUT, comparator_1_eq, WE_IN);
  and and_3 (RE_OUT, comparator_1_eq, RE_IN);
endmodule

module Binary_to_BCD (
  input  [15:0] Input,
  input  Load_Start,
  input  Reset,
  output [3:0] _10_000s,
  output [3:0] _1_000s,
  output [3:0] _100s,
  output [3:0] _10s,
  output [3:0] _1s
);

  wire binary_to_bcd_segment_2_out_5, binary_to_bcd_segment_3_out_5, binary_to_bcd_segment_4_out_5,
       binary_to_bcd_segment_5_out_5, clock_1_out, not_1_out, or_1_out, or_2_out, or_4_out,
       shift_register_1_p1, shift_register_1_p6;
  wire [4:0] multiplexer_1_out, register_1_q, subtractor_1_out;

  Clock clock_1 (.out(clock_1_out));
  not not_1 (not_1_out, Load_Start);
  Binary_to_BCD_Segment binary_to_bcd_segment_1 (
    .out_6(_10_000s), .in_1(binary_to_bcd_segment_2_out_5), ._CLR(not_1_out), .WE(shift_register_1_p1),
    .RESET(Reset));  // open: out_5
  Binary_to_BCD_Segment binary_to_bcd_segment_2 (
    .out_5(binary_to_bcd_segment_2_out_5), .out_6(_1_000s), .in_1(binary_to_bcd_segment_3_out_5),
    ._CLR(not_1_out), .WE(shift_register_1_p1), .RESET(Reset));
  Binary_to_BCD_Segment binary_to_bcd_segment_3 (
    .out_5(binary_to_bcd_segment_3_out_5), .out_6(_100s), .in_1(binary_to_bcd_segment_4_out_5),
    ._CLR(not_1_out), .WE(shift_register_1_p1), .RESET(Reset));
  Binary_to_BCD_Segment binary_to_bcd_segment_4 (
    .out_5(binary_to_bcd_segment_4_out_5), .out_6(_10s), .in_1(binary_to_bcd_segment_5_out_5),
    ._CLR(not_1_out), .WE(shift_register_1_p1), .RESET(Reset));
  Binary_to_BCD_Segment binary_to_bcd_segment_5 (
    .out_5(binary_to_bcd_segment_5_out_5), .out_6(_1s), .in_1(shift_register_1_p6), ._CLR(not_1_out),
    .WE(shift_register_1_p1), .RESET(Reset));
  // Shift_Register #(.length(16)) shift_register_1: pin names not known; wires that end beside it: shift_register_1_p1, 1'b0, clock_1_out, Load_Start, Reset, shift_register_1_p6
  Subtractor #(.width(5)) subtractor_1 (.a(register_1_q), .b(5'b00001), .out(subtractor_1_out));  // open: bin, bout
  Multiplexer #(.enable("false"), .width(5)) multiplexer_1 (
    .in0(subtractor_1_out), .in1(5'b10000), .out(multiplexer_1_out), .sel(Load_Start));
  or or_1 (or_1_out, Load_Start, shift_register_1_p1);
  Register #(.width(5)) register_1 (
    .D(multiplexer_1_out), .en(or_1_out), .clk(clock_1_out), .Q(register_1_q), .clr(Reset));
  or or_2 (or_2_out, register_1_q[0], register_1_q[1]);
  or or_3 (shift_register_1_p1, or_2_out, or_4_out);
  or or_4 (or_4_out, register_1_q[2], register_1_q[3], register_1_q[4]);
endmodule

module Binary_to_BCD_Segment (
  input  in_1,
  input  _CLR,
  input  WE,
  input  RESET,
  output out_5,
  output [3:0] out_6
);

  wire and_2_out, clock_1_out, not_1_out, or_1_out, or_2_out;
  wire [1:1] or_3_out;
  wire [2:0] adder_1_out;
  wire [3:0] and_1_out, bit_extender_1_out, register_1_q;

  assign and_1_out = {adder_1_out, in_1} & bit_extender_1_out;  // AND_Gate and_1, 4 bits wide
  assign bit_extender_1_out = {{3{_CLR}}, _CLR};  // Bit_Extender bit_extender_1
  not not_1 (not_1_out, _CLR);
  or or_1 (or_1_out, not_1_out, WE);
  Register #(.width(4)) register_1 (.D(and_1_out), .en(or_1_out), .clk(clock_1_out), .Q(register_1_q), .clr(RESET));
  Clock clock_1 (.out(clock_1_out));
  Register #(.trigger("falling"), .width(4)) register_2 (.D(register_1_q), .en(1'b1), .clk(WE), .Q(out_6), .clr(RESET));
  or or_2 (or_2_out, register_1_q[0], register_1_q[1]);
  and and_2 (and_2_out, or_2_out, register_1_q[2]);
  or or_3 (or_3_out[1], and_2_out, register_1_q[3]);
  Adder #(.width(4)) adder_1 (
    .a(register_1_q), .b({2'b00, {2{or_3_out[1]}}}), .out({out_5, adder_1_out}));  // open: cin, cout
endmodule

module Joystick_Processor (
  input  [15:0] Data_In,
  input  Reset,
  input  RE,
  output [15:0] Data_Out,
  output Interrupt
);

  wire clock_1_out, comparator_1_eq;
  wire [15:0] register_1_q, register_2_q;

  Clock clock_1 (.out(clock_1_out));
  Register #(.width(16)) register_1 (.D(Data_In), .en(1'b1), .clk(clock_1_out), .Q(register_1_q), .clr(Reset));
  Register #(.width(16)) register_2 (.D(register_1_q), .en(RE), .clk(clock_1_out), .Q(register_2_q), .clr(Reset));
  assign Data_Out = RE ? register_1_q : 16'bz;  // Controlled_Buffer controlled_buffer_1
  Comparator #(.mode("unsigned"), .width(16)) comparator_1 (
    .a(register_1_q), .b(register_2_q), .eq(comparator_1_eq));  // open: gt, lt
  not not_1 (Interrupt, comparator_1_eq);
endmodule

module Interrupt_Manager (
  input  Source_1,
  input  Source_2,
  input  Source_3,
  input  Source_4,
  input  Source_5,
  input  Source_6,
  input  Source_7,
  input  Source_8,
  input  Source_9,
  input  Source_10,
  input  Source_11,
  input  [15:0] Data_In,
  input  Source_12,
  input  Source_13,
  input  Source_14,
  input  Source_15,
  input  WE,
  input  [2:0] Register_Select,
  input  RE,
  input  Reset,
  output [15:0] Data_Out,
  output Interrupt
);

  wire adder_2_cout, and_2_out, and_3_out, bit_extender_2_out, clock_1_out, clock_2_out, clock_3_out,
       clock_4_out, clock_5_out, clock_6_out, clock_7_out, comparator_2_eq, nor_1_out, nor_2_out, not_1_out,
       not_2_out, or_1_out, or_2_out, or_3_out, or_4_out, or_5_out, or_6_out, or_7_out, or_8_out, or_9_out,
       priority_encoder_1_gs, RE2, RE3, RE4, RE5, RE6, RE7, register_1_q, register_3_q, subtractor_1_bout,
       TC_RESET, TIMER_ZERO, WE1, WE2, WE3, WE4, WE5, WE_RESET;
  wire [3:0] priority_encoder_1_out;
  wire [15:0] adder_1_out, adder_2_out, adder_3_out, and_4_out, and_6_out, and_7_out, bit_extender_3_out,
       DATA_EN, FREQ_HI, FREQ_LO, INT_SOURCE, TC_OUT, TICKS_HI, TICKS_LO, TIMER_HI, TIMER_LO, ZERO_DATA;
  wire [31:0] multiplexer_1_out, register_2_q, subtractor_1_out;

  Priority_Encoder #(.select(4)) priority_encoder_1 (
    .in0(Source_1), .in1(Source_2), .in2(Source_3), .in3(Source_4), .in4(Source_5), .in5(Source_6),
    .in6(Source_7), .in7(Source_8), .in8(Source_9), .in9(Source_10), .in10(Source_11), .in11(Source_12),
    .in12(Source_13), .in13(Source_14), .in14(Source_15), .in15(register_3_q), .out(priority_encoder_1_out),
    .gs(priority_encoder_1_gs));  // open: en_out, en_in
  and and_1 (Interrupt, priority_encoder_1_gs, register_1_q);
  Subtractor #(.width(32)) subtractor_1 (
    .a(register_2_q), .b({32{1'b0}}), .out(subtractor_1_out), .bin(1'b1), .bout(subtractor_1_bout));
  Comparator #(.mode("unsigned"), .width(32)) comparator_1 (
    .a(subtractor_1_out), .b({32{1'b0}}), .eq(TIMER_ZERO));  // open: gt, lt
  assign INT_SOURCE = {{12{1'b0}}, priority_encoder_1_out};  // Bit_Extender bit_extender_1
  Bit_Extender #(.in_width(16), .out_width(1), .\type ("zero")) bit_extender_2 (.in(Data_In), .out(bit_extender_2_out));
  or or_1 (or_1_out, WE_RESET, WE1);
  not not_1 (not_1_out, subtractor_1_bout);
  or or_2 (or_2_out, TC_RESET, WE_RESET);
  Register #(.width(1)) register_1 (.D(and_2_out), .en(or_1_out), .clk(clock_1_out), .Q(register_1_q), .clr(Reset));
  and and_2 (and_2_out, bit_extender_2_out, ~WE_RESET);  // AND_Gate
  Clock clock_1 (.out(clock_1_out));
  Multiplexer #(.enable("false"), .width(32)) multiplexer_1 (
    .in0({TIMER_HI, TIMER_LO}), .in1(subtractor_1_out), .out(multiplexer_1_out), .sel(not_1_out));
  Comparator #(.mode("unsigned"), .width(32)) comparator_2 (
    .a({TIMER_HI, TIMER_LO}), .b({32{1'b0}}), .eq(comparator_2_eq));  // open: gt, lt
  nor nor_1 (nor_1_out, register_3_q, or_2_out);
  or or_3 (or_3_out, TIMER_ZERO, or_2_out);
  Register #(.width(32)) register_2 (
    .D(multiplexer_1_out), .en(and_3_out), .clk(clock_2_out), .Q(register_2_q), .clr(Reset));
  Clock clock_2 (.out(clock_2_out));
  and and_3 (and_3_out, register_1_q, ~comparator_2_eq);  // AND_Gate
  Register #(.width(1)) register_3 (.D(nor_1_out), .en(or_3_out), .clk(clock_3_out), .Q(register_3_q), .clr(Reset));
  Clock clock_3 (.out(clock_3_out));
  Adder #(.width(16)) adder_1 (.a(TC_OUT), .b({16{1'b0}}), .out(adder_1_out), .cin(1'b1));  // open: cout
  nor nor_2 (nor_2_out, WE_RESET, TC_RESET);
  assign bit_extender_3_out = {{15{nor_2_out}}, nor_2_out};  // Bit_Extender bit_extender_3
  or or_4 (or_4_out, WE_RESET, TC_RESET, TIMER_ZERO);
  Demultiplexer #(.enable("false"), .select(3)) demultiplexer_1 (
    .out0(WE_RESET), .out1(WE1), .out2(WE2), .out3(WE3), .out4(WE4), .out5(WE5), .in(WE),
    .sel(Register_Select));  // open: out6, out7
  Demultiplexer #(.enable("false"), .select(3)) demultiplexer_2 (
    .out1(TC_RESET), .out2(RE2), .out3(RE3), .out4(RE4), .out5(RE5), .out6(RE6), .out7(RE7), .in(RE),
    .sel(Register_Select));  // open: out0
  not not_2 (not_2_out, WE_RESET);
  Register #(.width(16)) register_4 (.D(and_4_out), .en(or_4_out), .clk(clock_4_out), .Q(TC_OUT), .clr(Reset));
  assign and_4_out = adder_1_out & bit_extender_3_out;  // AND_Gate and_4, 16 bits wide
  Clock clock_4 (.out(clock_4_out));
  assign ZERO_DATA = {{15{not_2_out}}, not_2_out};  // Bit_Extender bit_extender_4
  assign DATA_EN = Data_In & ZERO_DATA;  // AND_Gate and_5, 16 bits wide
  Adder #(.width(16)) adder_2 (.a(TICKS_LO), .b({16{1'b0}}), .out(adder_2_out), .cin(1'b1), .cout(adder_2_cout));
  Adder #(.width(16)) adder_3 (.a(TICKS_HI), .b({16{1'b0}}), .out(adder_3_out), .cin(adder_2_cout));  // open: cout
  assign and_6_out = adder_2_out & ZERO_DATA;  // AND_Gate and_6, 16 bits wide
  or or_5 (or_5_out, WE_RESET, TIMER_ZERO);
  assign and_7_out = adder_3_out & ZERO_DATA;  // AND_Gate and_7, 16 bits wide
  Clock clock_5 (.out(clock_5_out));
  Multiplexer #(.disabled("Z"), .select(3), .width(16)) multiplexer_2 (
    .in0(INT_SOURCE), .in1(TC_OUT), .in2(FREQ_LO), .in3(FREQ_HI), .in4(TIMER_LO), .in5(TIMER_HI),
    .in6(TICKS_LO), .in7(TICKS_HI), .out(Data_Out), .sel(Register_Select), .en(RE));
  Register #(.width(16)) register_5 (.D(DATA_EN), .en(or_6_out), .clk(clock_6_out), .Q(FREQ_LO), .clr(Reset));
  or or_6 (or_6_out, WE_RESET, WE4);
  Clock clock_6 (.out(clock_6_out));
  Register #(.width(16)) register_6 (.D(DATA_EN), .en(or_7_out), .clk(clock_6_out), .Q(FREQ_HI), .clr(Reset));
  or or_7 (or_7_out, WE_RESET, WE5);
  Register #(.width(16)) register_7 (.D(DATA_EN), .en(or_8_out), .clk(clock_7_out), .Q(TIMER_LO), .clr(Reset));
  or or_8 (or_8_out, WE_RESET, WE4);
  Clock clock_7 (.out(clock_7_out));
  Register #(.width(16)) register_8 (.D(DATA_EN), .en(or_9_out), .clk(clock_7_out), .Q(TIMER_HI), .clr(Reset));
  or or_9 (or_9_out, WE_RESET, WE5);
  Register #(.width(16)) register_9 (.D(and_6_out), .en(or_5_out), .clk(clock_5_out), .Q(TICKS_LO), .clr(Reset));
  Register #(.width(16)) register_10 (.D(and_7_out), .en(or_5_out), .clk(clock_5_out), .Q(TICKS_HI), .clr(Reset));

  // Other names for the same wires on the sheet: PIN_RESET = Reset; RS[2:0] = Register_Select

  // Notes on the sheet:
  //   Registers:
  //   	0:	Interrupt Source
  //   	1:	Configuration
  //   	2:	Frequency Low
  //   	3:	Frequency High
  //   	4:	Timer Low
  //   	5:	Timer High
  //   	6:	Clocks Low
  //   	7:	Clocks High
  //   Write Response:
  //   	0:	Reset
  //   Read Response:
  //   	1:	Ack Timers
  //   		  #Timer Laps
endmodule
